# Fritzing sketch circuit (saved by Fritzing 0.7.7b)
breadboards: 1

parts:
  Arduino1 = Arduino
  R1 = Resistor [tolerance=±5% resistance=1.5k package=THT]
  LED1 = LED - 5mm [color="Red (633nm)" package="5 mm [THT]"]

nets:
  N1: Arduino1.GND, LED1.cathode
  N2: Arduino1.D3, R1.Pin_0
  N3: R1.Pin_1, LED1.anode
